// Logisim project reproject.circ as structural Verilog: 5 circuits, main circuit main
module main (
);

  _1_bit_alu u_1_bit_alu_1 ();  // open: a, Ain, b, Bin, result, cin, cout, aluop
  _16_bit_alu u_16_bit_alu_1 ();  // open: result, a, aluop, Ain, Bin, b, cin, zero_detector, overflow
endmodule

module _1_bit_alu (
  input  cin,
  input  a,
  input  Ain,
  input  [1:0] aluop,
  input  b,
  input  Bin,
  output result,
  output cout
);

  wire adder_1_out, and_1_out, multiplexer_1_out, multiplexer_2_out, not_1_out, not_2_out, or_1_out;

  not not_1 (not_1_out, a);
  not not_2 (not_2_out, b);
  Multiplexer #(.enable("false")) multiplexer_1 (.in0(a), .in1(not_1_out), .out(multiplexer_1_out), .sel(Ain));
  Multiplexer #(.enable("false")) multiplexer_2 (.in0(b), .in1(not_2_out), .out(multiplexer_2_out), .sel(Bin));
  and and_1 (and_1_out, multiplexer_1_out, multiplexer_2_out);
  or or_1 (or_1_out, multiplexer_1_out, multiplexer_2_out);
  Adder #(.width(1)) adder_1 (.a(multiplexer_1_out), .b(multiplexer_2_out), .out(adder_1_out), .cin(cin), .cout(cout));
  Multiplexer #(.select(2), .enable("false")) multiplexer_3 (
    .in0(and_1_out), .in1(or_1_out), .in2(adder_1_out), .out(result), .sel(aluop));  // open: in3
endmodule

module _16_bit_alu (
  input  [15:0] a,
  input  cin,
  input  [1:0] aluop,
  input  Ain,
  input  Bin,
  input  [15:0] b,
  output [15:0] result,
  output zero_detector,
  output overflow
);

  wire n1_bit_alu_1_cout, n1_bit_alu_2_cout, n1_bit_alu_3_cout, n1_bit_alu_4_cout, n1_bit_alu_5_cout,
       n1_bit_alu_6_cout, n1_bit_alu_7_cout, n1_bit_alu_8_cout, n1_bit_alu_9_cout, n1_bit_alu_10_cout,
       n1_bit_alu_11_cout, n1_bit_alu_12_cout, n1_bit_alu_13_cout, n1_bit_alu_14_cout, n1_bit_alu_15_cout,
       n1_bit_alu_16_cout;

  _1_bit_alu u_1_bit_alu_1 (
    .a(a[0]), .Ain(Ain), .b(b[0]), .Bin(Bin), .result(result[0]), .cin(cin), .cout(n1_bit_alu_1_cout),
    .aluop(aluop));
  _1_bit_alu u_1_bit_alu_2 (
    .a(a[1]), .Ain(Ain), .b(b[1]), .Bin(Bin), .result(result[1]), .cin(n1_bit_alu_1_cout),
    .cout(n1_bit_alu_2_cout), .aluop(aluop));
  _1_bit_alu u_1_bit_alu_3 (
    .a(a[2]), .Ain(Ain), .b(b[2]), .Bin(Bin), .result(result[2]), .cin(n1_bit_alu_2_cout),
    .cout(n1_bit_alu_3_cout), .aluop(aluop));
  _1_bit_alu u_1_bit_alu_4 (
    .a(a[3]), .Ain(Ain), .b(b[3]), .Bin(Bin), .result(result[3]), .cin(n1_bit_alu_3_cout),
    .cout(n1_bit_alu_4_cout), .aluop(aluop));
  _1_bit_alu u_1_bit_alu_5 (
    .a(a[4]), .Ain(Ain), .b(b[4]), .Bin(Bin), .result(result[4]), .cin(n1_bit_alu_4_cout),
    .cout(n1_bit_alu_5_cout), .aluop(aluop));
  _1_bit_alu u_1_bit_alu_6 (
    .a(a[5]), .Ain(Ain), .b(b[5]), .Bin(Bin), .result(result[5]), .cin(n1_bit_alu_5_cout),
    .cout(n1_bit_alu_6_cout), .aluop(aluop));
  _1_bit_alu u_1_bit_alu_7 (
    .a(a[6]), .Ain(Ain), .b(b[6]), .Bin(Bin), .result(result[6]), .cin(n1_bit_alu_6_cout),
    .cout(n1_bit_alu_7_cout), .aluop(aluop));
  _1_bit_alu u_1_bit_alu_8 (
    .a(a[7]), .Ain(Ain), .b(b[7]), .Bin(Bin), .result(result[7]), .cin(n1_bit_alu_7_cout),
    .cout(n1_bit_alu_8_cout), .aluop(aluop));
  _1_bit_alu u_1_bit_alu_9 (
    .a(a[8]), .Ain(Ain), .b(b[8]), .Bin(Bin), .result(result[8]), .cin(n1_bit_alu_8_cout),
    .cout(n1_bit_alu_9_cout), .aluop(aluop));
  _1_bit_alu u_1_bit_alu_10 (
    .a(a[9]), .Ain(Ain), .b(b[9]), .Bin(Bin), .result(result[9]), .cin(n1_bit_alu_9_cout),
    .cout(n1_bit_alu_10_cout), .aluop(aluop));
  _1_bit_alu u_1_bit_alu_11 (
    .a(a[10]), .Ain(Ain), .b(b[10]), .Bin(Bin), .result(result[10]), .cin(n1_bit_alu_10_cout),
    .cout(n1_bit_alu_11_cout), .aluop(aluop));
  _1_bit_alu u_1_bit_alu_12 (
    .a(a[11]), .Ain(Ain), .b(b[11]), .Bin(Bin), .result(result[11]), .cin(n1_bit_alu_11_cout),
    .cout(n1_bit_alu_12_cout), .aluop(aluop));
  _1_bit_alu u_1_bit_alu_13 (
    .a(a[12]), .Ain(Ain), .b(b[12]), .Bin(Bin), .result(result[12]), .cin(n1_bit_alu_12_cout),
    .cout(n1_bit_alu_13_cout), .aluop(aluop));
  _1_bit_alu u_1_bit_alu_14 (
    .a(a[13]), .Ain(Ain), .b(b[13]), .Bin(Bin), .result(result[13]), .cin(n1_bit_alu_13_cout),
    .cout(n1_bit_alu_14_cout), .aluop(aluop));
  _1_bit_alu u_1_bit_alu_15 (
    .a(a[14]), .Ain(Ain), .b(b[14]), .Bin(Bin), .result(result[14]), .cin(n1_bit_alu_14_cout),
    .cout(n1_bit_alu_15_cout), .aluop(aluop));
  _1_bit_alu u_1_bit_alu_16 (
    .a(a[15]), .Ain(Ain), .b(b[15]), .Bin(Bin), .result(result[15]), .cin(n1_bit_alu_15_cout),
    .cout(n1_bit_alu_16_cout), .aluop(aluop));
  xor xor_1 (overflow, n1_bit_alu_15_cout, n1_bit_alu_16_cout);
  nor nor_1 (zero_detector, result[0], result[1], result[2], result[3], result[4], result[5], result[6], result[7], result[8], result[9], result[10], result[11], result[12], result[13], result[14], result[15]);
endmodule

module test_ic (
  input  aluop,
  input  aluop_2,
  input  aluop_3,
  input  [1:0] aluop_4,
  input  aluop_5,
  input  aluop_6,
  output out_7,
  output out_8
);

  _1_bit_alu u_1_bit_alu_1 (
    .a(aluop), .Ain(aluop_5), .b(aluop_3), .Bin(aluop_6), .result(out_7), .cin(aluop_2), .cout(out_8),
    .aluop(aluop_4));
endmodule

module _16_bit_alu_test (
  input  [1:0] aluop,
  input  cin,
  input  [15:0] a,
  input  [15:0] b,
  input  Ain,
  input  Bin,
  output out_7,
  output [15:0] out_8,
  output out_9
);

  _16_bit_alu u_16_bit_alu_1 (
    .result(out_8), .a(a), .aluop(aluop), .Ain(Ain), .Bin(Bin), .b(b), .cin(cin), .zero_detector(out_7),
    .overflow(out_9));
endmodule
